// Logisim project mips.circ as structural Verilog: 14 circuits, main circuit mips
module latch (
  input  Reset,
  input  Set,
  output Q,
  output nQ
);

  nor nor_1 (Q, Reset, nQ);
  nor nor_2 (nQ, Q, Set);
endmodule

module latchClock (
  input  reset,
  input  Clock,
  input  set,
  output Y,
  output out_5
);

  wire and_1_out, and_2_out, and_3_out, and_4_out, and_5_out, latch_1_q;

  and and_1 (and_1_out, reset, Clock);
  and and_2 (and_2_out, Clock, set);
  latch latch_1 (.Reset(and_1_out), .Set(and_2_out), .Q(latch_1_q), .nQ(out_5));
  and and_3 (and_3_out, ~and_1_out, ~and_2_out, latch_1_q);  // AND_Gate
  and and_4 (and_4_out, ~and_1_out, and_2_out, latch_1_q);  // AND_Gate
  and and_5 (and_5_out, and_2_out, and_1_out, ~latch_1_q);  // AND_Gate
  or or_1 (Y, and_3_out, and_4_out, and_5_out);

  // Notes on the sheet:
  //   L
endmodule

module latchD (
  input  D,
  input  Write,
  output out_3,
  output out_4
);

  wire not_1_out;

  not not_1 (not_1_out, D);
  latchClock latchclock_1 (.reset(not_1_out), .Clock(Write), .set(D), .Y(out_3), .out_5(out_4));
endmodule

module registro8bit (
  input  clock,
  input  reset,
  input  [7:0] data_input,
  output [7:0] \output 
);

  D_Flip_Flop d_ff_1 (.clk(clock), .D(data_input[7]), .Q(\output [7]), .reset(reset));  // open: Qn, preset, en
  D_Flip_Flop d_ff_2 (.clk(clock), .D(data_input[6]), .Q(\output [6]), .reset(reset));  // open: Qn, preset, en
  D_Flip_Flop d_ff_3 (.clk(clock), .D(data_input[5]), .Q(\output [5]), .reset(reset));  // open: Qn, preset, en
  D_Flip_Flop d_ff_4 (.clk(clock), .D(data_input[3]), .Q(\output [3]), .reset(reset));  // open: Qn, preset, en
  D_Flip_Flop d_ff_5 (.clk(clock), .D(data_input[4]), .Q(\output [4]), .reset(reset));  // open: Qn, preset, en
  D_Flip_Flop d_ff_6 (.clk(clock), .D(data_input[2]), .Q(\output [2]), .reset(reset));  // open: Qn, preset, en
  D_Flip_Flop d_ff_7 (.clk(clock), .D(data_input[1]), .Q(\output [1]), .reset(reset));  // open: Qn, preset, en
  D_Flip_Flop d_ff_8 (.clk(clock), .D(data_input[0]), .Q(\output [0]), .reset(reset));  // open: Qn, preset, en

  // Other names for the same wires on the sheet: d7 = data_input[0]; d6 = data_input[1]; d5 = data_input[2];
  //   d4 = data_input[3]; d3 = data_input[4]; d2 = data_input[5]; d1 = data_input[6]; d0 = data_input[7];
  //   dO7 = \output [0]; dO6 = \output [1]; dO5 = \output [2]; dO4 = \output [3]; dO3 = \output [4];
  //   dO2 = \output [5]; dO1 = \output [6]; dO0 = \output [7]
endmodule

module complementoA2 (
  input  [7:0] in_1,
  output [7:0] out_2
);

  wire [7:0] not_1_out;

  assign not_1_out = ~in_1;  // NOT_Gate not_1, 8 bits wide
  Adder adder_1 (.a(8'h1), .b(not_1_out), .out(out_2));  // open: cin, cout
endmodule

module divisore8bit (
  input  in_1,
  input  [7:0] A,
  input  [7:0] B,
  output [7:0] out_4,
  output [7:0] out_5,
  output [7:0] out_6
);

  wire clock, or_1_out;
  wire [2:0] counter_1_q;
  wire [3:3] counter_1_q_2;
  wire [7:0] adder_1_out, adder_2_out, multiplexer_2_out, multiplexer_3_out, not_1_out, shifter_1_out,
       shifter_2_out;

  Clock clock_1 (.out(clock));
  Adder adder_1 (.a(out_6), .b(not_1_out), .out(adder_1_out), .cin(1'b1));  // open: cout
  assign not_1_out = ~shifter_1_out;  // NOT_Gate not_1, 8 bits wide
  Shifter #(.shift("lr")) shifter_1 (.in(B), .\dist (counter_1_q), .out(shifter_1_out));
  Multiplexer #(.width(8), .enable("false")) multiplexer_1 (.in0(A), .in1(adder_1_out), .out(out_4), .sel(or_1_out));
  or or_1 (or_1_out, counter_1_q_2[3], counter_1_q[2], counter_1_q[1], counter_1_q[0]);
  Counter #(.width(4), .max('h9), .ongoal("stay")) counter_1 (
    .D({counter_1_q_2[3], counter_1_q}), .count(1'b1), .Q({counter_1_q_2[3], counter_1_q}), .clk(clock),
    .clr(in_1));  // open: load, carry
  registro8bit registro8bit_1 (.clock(clock), .reset(in_1), .data_input(multiplexer_2_out), .\output (out_5));
  // NOT_Gate not_2 is placed but not wired
  Shifter shifter_2 (.in(out_5), .\dist (3'b001), .out(shifter_2_out));
  Adder adder_2 (.a(8'h1), .b(shifter_2_out), .out(adder_2_out));  // open: cin, cout
  Multiplexer #(.width(8), .enable("false")) multiplexer_2 (
    .in0(adder_2_out), .in1(shifter_2_out), .out(multiplexer_2_out), .sel(out_4[7]));
  Multiplexer #(.width(8), .enable("false")) multiplexer_3 (
    .in0(out_4), .in1(out_6), .out(multiplexer_3_out), .sel(out_4[7]));
  registro8bit registro8bit_2 (.clock(clock), .reset(in_1), .data_input(multiplexer_3_out), .\output (out_6));

  // Other names for the same wires on the sheet: reset = in_1; RP[7:0] = out_6; RP_B[7:0] = out_4
endmodule

module flipflop (
  input  in_1,
  input  in_2,
  output Q,
  output nQ
);

  wire latchd_2_out_3, not_1_out;

  latchD latchd_1 (.D(latchd_2_out_3), .Write(not_1_out), .out_3(Q), .out_4(nQ));
  latchD latchd_2 (.D(in_1), .Write(in_2), .out_3(latchd_2_out_3));  // open: out_4
  not not_1 (not_1_out, in_2);
endmodule

module mips (
);

  wire clock_1_out, init_q, not_1_out, UC_alusrc, UC_mem2reg, UC_memread, UC_memwrite, UC_regdst,
       UC_regwrite, zero;
  wire [1:0] UC_branch;
  wire [2:0] UC_ALU_aluop, UC_alus;
  wire [4:0] multiplexer_2_out;
  wire [27:0] rom_1_data, shifter_1_out;
  wire [31:0] adder_1_out, adder_2_out, ALU_out_5, es_segno_out_2, multiplexer_1_out, multiplexer_3_out,
       multiplexer_4_out, multiplexer_5_out, PC_out_3, ram_1_data, registers_1_dataread1,
       registers_1_dataread2, shifter_2_out;
  wire [31:28] rom_1_data_2;

  not not_1 (not_1_out, clock_1_out);
  Clock clock_1 (.out(clock_1_out));
  Multiplexer #(.width(32), .enable("false")) multiplexer_1 (
    .in0({32{1'b0}}), .in1(multiplexer_4_out), .out(multiplexer_1_out), .sel(init_q));
  D_Flip_Flop init (.clk(not_1_out), .D(1'b1), .Q(init_q));  // open: Qn, preset, en, reset
  _32bitflipflop PC (.in_1(multiplexer_1_out), .in_2(clock_1_out), .out_3(PC_out_3));
  Adder #(.width(32)) adder_1 (.a(PC_out_3), .b(32'h4), .out(adder_1_out));  // open: cin, cout
  Shifter #(.width(28)) shifter_1 (.in(rom_1_data), .\dist (5'b00010), .out(shifter_1_out));
  ROM #(.addrWidth(24), .dataWidth(32)) rom_1 (.addr(PC_out_3[25:2]), .data({rom_1_data_2, rom_1_data}));  // open: sel
  UC UC (
    .OpCode({rom_1_data_2, rom_1_data[27:26]}), .J(UC_branch[1]), .RegDst(UC_regdst), .Branch(UC_branch[0]),
    .MemRead(UC_memread), .Mem2Reg(UC_mem2reg), .ALUs(UC_alus), .zero(zero), .MemWrite(UC_memwrite),
    .ALUSrc(UC_alusrc), .RegWrite(UC_regwrite));
  Multiplexer #(.width(5), .enable("false")) multiplexer_2 (
    .in0(rom_1_data[20:16]), .in1(rom_1_data[15:11]), .out(multiplexer_2_out), .sel(UC_regdst));
  estensione_del_segno es_segno (.in_1(rom_1_data[15:0]), .out_2(es_segno_out_2));
  Shifter #(.width(32)) shifter_2 (.in(es_segno_out_2), .\dist (5'b00010), .out(shifter_2_out));
  registers registers_1 (
    .DataWr(multiplexer_5_out), .Write(UC_regwrite), .Clock(clock_1_out), .RegWrite(multiplexer_2_out),
    .RegRead1(rom_1_data[25:21]), .RegRead2(rom_1_data[20:16]), .DataRead2(registers_1_dataread2),
    .DataRead1(registers_1_dataread1));
  Adder #(.width(32)) adder_2 (.a(adder_1_out), .b(shifter_2_out), .out(adder_2_out));  // open: cin, cout
  alu ALU (
    .in_1(registers_1_dataread1), .out_5(ALU_out_5), .in_2(multiplexer_3_out), .ALUop(UC_ALU_aluop),
    .zero(zero));
  Multiplexer #(.width(32), .enable("false")) multiplexer_3 (
    .in0(registers_1_dataread2), .in1(es_segno_out_2), .out(multiplexer_3_out), .sel(UC_alusrc));
  UC_ALU UC_ALU (.Funct(rom_1_data[5:0]), .ALUs(UC_alus), .ALUop(UC_ALU_aluop));
  Multiplexer #(.select(2), .width(32), .enable("false")) multiplexer_4 (
    .in0(adder_1_out), .in1(adder_2_out), .in2({PC_out_3[31:28], shifter_1_out}), .out(multiplexer_4_out),
    .sel(UC_branch));  // open: in3
  RAM #(.addrWidth(24), .dataWidth(32), .bus("separate")) ram_1 (
    .addr(ALU_out_5[23:0]), .din(registers_1_dataread2), .data(ram_1_data), .str(UC_memwrite),
    .clk(clock_1_out), .ld(UC_memread));  // open: sel, clr
  Multiplexer #(.width(32), .enable("false")) multiplexer_5 (
    .in0(ALU_out_5), .in1(ram_1_data), .out(multiplexer_5_out), .sel(UC_mem2reg));

  // Notes on the sheet:
  //   contents of rom_1 (hex, n*v repeats v):
  //   20080003 ac080064 20080005 ac080068 20080008 ac08006c 2008000f ac080070 20080012 ac080074 20080017
  //   ac080078 20050005 20060018 20040064 20020000 10c00007 c44020 2108fffc 8d080000 11050002 20c6fffc
  //   800000f 20020001
endmodule

module _32bitflipflop (
  input  [31:0] in_1,
  input  in_2,
  output [31:0] out_3
);

  flipflop flipflop_1 (.in_1(in_1[24]), .in_2(in_2), .Q(out_3[24]));  // open: nQ
  flipflop flipflop_2 (.in_1(in_1[25]), .in_2(in_2), .Q(out_3[25]));  // open: nQ
  flipflop flipflop_3 (.in_1(in_1[26]), .in_2(in_2), .Q(out_3[26]));  // open: nQ
  flipflop flipflop_4 (.in_1(in_1[27]), .in_2(in_2), .Q(out_3[27]));  // open: nQ
  flipflop flipflop_5 (.in_1(in_1[28]), .in_2(in_2), .Q(out_3[28]));  // open: nQ
  flipflop flipflop_6 (.in_1(in_1[29]), .in_2(in_2), .Q(out_3[29]));  // open: nQ
  flipflop flipflop_7 (.in_1(in_1[30]), .in_2(in_2), .Q(out_3[30]));  // open: nQ
  flipflop flipflop_8 (.in_1(in_1[31]), .in_2(in_2), .Q(out_3[31]));  // open: nQ
  flipflop flipflop_9 (.in_1(in_1[16]), .in_2(in_2), .Q(out_3[16]));  // open: nQ
  flipflop flipflop_10 (.in_1(in_1[17]), .in_2(in_2), .Q(out_3[17]));  // open: nQ
  flipflop flipflop_11 (.in_1(in_1[18]), .in_2(in_2), .Q(out_3[18]));  // open: nQ
  flipflop flipflop_12 (.in_1(in_1[19]), .in_2(in_2), .Q(out_3[19]));  // open: nQ
  flipflop flipflop_13 (.in_1(in_1[20]), .in_2(in_2), .Q(out_3[20]));  // open: nQ
  flipflop flipflop_14 (.in_1(in_1[21]), .in_2(in_2), .Q(out_3[21]));  // open: nQ
  flipflop flipflop_15 (.in_1(in_1[22]), .in_2(in_2), .Q(out_3[22]));  // open: nQ
  flipflop flipflop_16 (.in_1(in_1[23]), .in_2(in_2), .Q(out_3[23]));  // open: nQ
  flipflop flipflop_17 (.in_1(in_1[8]), .in_2(in_2), .Q(out_3[8]));  // open: nQ
  flipflop flipflop_18 (.in_1(in_1[9]), .in_2(in_2), .Q(out_3[9]));  // open: nQ
  flipflop flipflop_19 (.in_1(in_1[10]), .in_2(in_2), .Q(out_3[10]));  // open: nQ
  flipflop flipflop_20 (.in_1(in_1[11]), .in_2(in_2), .Q(out_3[11]));  // open: nQ
  flipflop flipflop_21 (.in_1(in_1[12]), .in_2(in_2), .Q(out_3[12]));  // open: nQ
  flipflop flipflop_22 (.in_1(in_1[13]), .in_2(in_2), .Q(out_3[13]));  // open: nQ
  flipflop flipflop_23 (.in_1(in_1[14]), .in_2(in_2), .Q(out_3[14]));  // open: nQ
  flipflop flipflop_24 (.in_1(in_1[15]), .in_2(in_2), .Q(out_3[15]));  // open: nQ
  flipflop flipflop_25 (.in_1(in_1[0]), .in_2(in_2), .Q(out_3[0]));  // open: nQ
  flipflop flipflop_26 (.in_1(in_1[1]), .in_2(in_2), .Q(out_3[1]));  // open: nQ
  flipflop flipflop_27 (.in_1(in_1[2]), .in_2(in_2), .Q(out_3[2]));  // open: nQ
  flipflop flipflop_28 (.in_1(in_1[3]), .in_2(in_2), .Q(out_3[3]));  // open: nQ
  flipflop flipflop_29 (.in_1(in_1[4]), .in_2(in_2), .Q(out_3[4]));  // open: nQ
  flipflop flipflop_30 (.in_1(in_1[5]), .in_2(in_2), .Q(out_3[5]));  // open: nQ
  flipflop flipflop_31 (.in_1(in_1[6]), .in_2(in_2), .Q(out_3[6]));  // open: nQ
  flipflop flipflop_32 (.in_1(in_1[7]), .in_2(in_2), .Q(out_3[7]));  // open: nQ
endmodule

module UC (
  input  [5:0] OpCode,
  input  zero,
  output RegDst,
  output J,
  output Branch,
  output MemRead,
  output Mem2Reg,
  output [2:0] ALUs,
  output MemWrite,
  output ALUSrc,
  output RegWrite
);

  wire addi_out, and_1_out, and_2_out, andi_out, beq_out, bne_out, ori_out, slti_out;

  and slti (slti_out, ~OpCode[0], OpCode[1], ~OpCode[2], OpCode[3], ~OpCode[4], ~OpCode[5]);  // AND_Gate
  and andi (andi_out, ~OpCode[0], ~OpCode[1], OpCode[2], OpCode[3], ~OpCode[4], ~OpCode[5]);  // AND_Gate
  and ori (ori_out, OpCode[0], ~OpCode[1], OpCode[2], OpCode[3], ~OpCode[4], ~OpCode[5]);  // AND_Gate
  and addi (addi_out, ~OpCode[0], ~OpCode[1], ~OpCode[2], OpCode[3], ~OpCode[4], ~OpCode[5]);  // AND_Gate
  and istr__R (RegDst, ~OpCode[0], ~OpCode[1], ~OpCode[2], ~OpCode[3], ~OpCode[4], ~OpCode[5]);  // AND_Gate
  and bne (bne_out, OpCode[0], ~OpCode[1], OpCode[2], ~OpCode[3], ~OpCode[4], ~OpCode[5]);  // AND_Gate
  and beq (beq_out, ~OpCode[0], ~OpCode[1], OpCode[2], ~OpCode[3], ~OpCode[4], ~OpCode[5]);  // AND_Gate
  and lw (Mem2Reg, OpCode[0], OpCode[1], ~OpCode[2], ~OpCode[3], ~OpCode[4], OpCode[5]);  // AND_Gate
  and sw (MemWrite, OpCode[0], OpCode[1], ~OpCode[2], OpCode[3], ~OpCode[4], OpCode[5]);  // AND_Gate
  and u_j (J, ~OpCode[0], OpCode[1], ~OpCode[2], ~OpCode[3], ~OpCode[4], ~OpCode[5]);  // AND_Gate
  and and_1 (and_1_out, beq_out, zero);
  and and_2 (and_2_out, ~zero, bne_out);  // AND_Gate
  or or_1 (Branch, and_1_out, and_2_out);
  or or_2 (ALUs[0], MemWrite, Mem2Reg, addi_out, ori_out, slti_out);
  or or_3 (ALUs[1], MemWrite, Mem2Reg, beq_out, bne_out, RegDst, addi_out, slti_out);
  or or_4 (ALUs[2], beq_out, bne_out, slti_out);
  or or_5 (ALUSrc, MemWrite, Mem2Reg, addi_out, ori_out, andi_out, slti_out);
  or or_6 (RegWrite, RegDst, Mem2Reg, addi_out, ori_out, andi_out, slti_out);

  assign MemRead = Mem2Reg;
endmodule

// Registri
module registers (
  input  [31:0] DataWr,
  input  Write,
  input  Clock,
  input  [4:0] RegWrite,
  input  [4:0] RegRead1,
  input  [4:0] RegRead2,
  output [31:0] DataRead2,
  output [31:0] DataRead1
);

  wire and_1_out;
  wire [31:0] _0, _1, _2, _3, _4, _5, _6, _7, _8, _9, _10, _11, _12, _13, _14, _15, _16, _17, _18, _19, _20,
       _21, _22, _23, _24, _25, _26, _27, _28, _29, _30, _31, demultiplexer_1_out0;

  and and_1 (and_1_out, Write, Clock);
  Demultiplexer #(.select(5), .enable("false")) demultiplexer_1 (
    .out0(demultiplexer_1_out0[0]), .out1(demultiplexer_1_out0[1]), .out2(demultiplexer_1_out0[2]),
    .out3(demultiplexer_1_out0[3]), .out4(demultiplexer_1_out0[4]), .out5(demultiplexer_1_out0[5]),
    .out6(demultiplexer_1_out0[6]), .out7(demultiplexer_1_out0[7]), .out8(demultiplexer_1_out0[8]),
    .out9(demultiplexer_1_out0[9]), .out10(demultiplexer_1_out0[10]), .out11(demultiplexer_1_out0[11]),
    .out12(demultiplexer_1_out0[12]), .out13(demultiplexer_1_out0[13]), .out14(demultiplexer_1_out0[14]),
    .out15(demultiplexer_1_out0[15]), .out16(demultiplexer_1_out0[16]), .out17(demultiplexer_1_out0[17]),
    .out18(demultiplexer_1_out0[18]), .out19(demultiplexer_1_out0[19]), .out20(demultiplexer_1_out0[20]),
    .out21(demultiplexer_1_out0[21]), .out22(demultiplexer_1_out0[22]), .out23(demultiplexer_1_out0[23]),
    .out24(demultiplexer_1_out0[24]), .out25(demultiplexer_1_out0[25]), .out26(demultiplexer_1_out0[26]),
    .out27(demultiplexer_1_out0[27]), .out28(demultiplexer_1_out0[28]), .out29(demultiplexer_1_out0[29]),
    .out30(demultiplexer_1_out0[30]), .out31(demultiplexer_1_out0[31]), .in(and_1_out), .sel(RegWrite));
  Register #(.width(32)) zero (.D(DataWr), .Q(_0), .clk(demultiplexer_1_out0[0]));  // open: en, clr
  Register #(.width(32)) t0 (.D(DataWr), .Q(_8), .clk(demultiplexer_1_out0[8]));  // open: en, clr
  Register #(.width(32)) s0 (.D(DataWr), .Q(_16), .clk(demultiplexer_1_out0[16]));  // open: en, clr
  Register #(.width(32)) t8 (.D(DataWr), .Q(_24), .clk(demultiplexer_1_out0[24]));  // open: en, clr
  Multiplexer #(.select(5), .width(32), .enable("false")) multiplexer_1 (
    .in0(_0), .in1(_1), .in2(_2), .in3(_3), .in4(_4), .in5(_5), .in6(_6), .in7(_7), .in8(_8), .in9(_9),
    .in10(_10), .in11(_11), .in12(_12), .in13(_13), .in14(_14), .in15(_15), .in16(_16), .in17(_17),
    .in18(_18), .in19(_19), .in20(_20), .in21(_21), .in22(_22), .in23(_23), .in24(_24), .in25(_25),
    .in26(_26), .in27(_27), .in28(_28), .in29(_29), .in30(_30), .in31(_31), .out(DataRead1), .sel(RegRead1));
  Register #(.width(32)) at (.D(DataWr), .Q(_1), .clk(demultiplexer_1_out0[1]));  // open: en, clr
  Register #(.width(32)) t1 (.D(DataWr), .Q(_9), .clk(demultiplexer_1_out0[9]));  // open: en, clr
  Register #(.width(32)) s1 (.D(DataWr), .Q(_17), .clk(demultiplexer_1_out0[17]));  // open: en, clr
  Register #(.width(32)) t9 (.D(DataWr), .Q(_25), .clk(demultiplexer_1_out0[25]));  // open: en, clr
  Register #(.width(32)) v0 (.D(DataWr), .Q(_2), .clk(demultiplexer_1_out0[2]));  // open: en, clr
  Register #(.width(32)) t2 (.D(DataWr), .Q(_10), .clk(demultiplexer_1_out0[10]));  // open: en, clr
  Register #(.width(32)) s2 (.D(DataWr), .Q(_18), .clk(demultiplexer_1_out0[18]));  // open: en, clr
  Register #(.width(32)) k0 (.D(DataWr), .Q(_26), .clk(demultiplexer_1_out0[26]));  // open: en, clr
  Register #(.width(32)) v1 (.D(DataWr), .Q(_3), .clk(demultiplexer_1_out0[3]));  // open: en, clr
  Register #(.width(32)) t3 (.D(DataWr), .Q(_11), .clk(demultiplexer_1_out0[11]));  // open: en, clr
  Register #(.width(32)) s3 (.D(DataWr), .Q(_19), .clk(demultiplexer_1_out0[19]));  // open: en, clr
  Register #(.width(32)) k1 (.D(DataWr), .Q(_27), .clk(demultiplexer_1_out0[27]));  // open: en, clr
  Multiplexer #(.select(5), .width(32), .enable("false")) multiplexer_2 (
    .in0(_0), .in1(_1), .in2(_2), .in3(_3), .in4(_4), .in5(_5), .in6(_6), .in7(_7), .in8(_8), .in9(_9),
    .in10(_10), .in11(_11), .in12(_12), .in13(_13), .in14(_14), .in15(_15), .in16(_16), .in17(_17),
    .in18(_18), .in19(_19), .in20(_20), .in21(_21), .in22(_22), .in23(_23), .in24(_24), .in25(_25),
    .in26(_26), .in27(_27), .in28(_28), .in29(_29), .in30(_30), .in31(_31), .out(DataRead2), .sel(RegRead2));
  Register #(.width(32)) a0 (.D(DataWr), .Q(_4), .clk(demultiplexer_1_out0[4]));  // open: en, clr
  Register #(.width(32)) t4 (.D(DataWr), .Q(_12), .clk(demultiplexer_1_out0[12]));  // open: en, clr
  Register #(.width(32)) s4 (.D(DataWr), .Q(_20), .clk(demultiplexer_1_out0[20]));  // open: en, clr
  Register #(.width(32)) gp (.D(DataWr), .Q(_28), .clk(demultiplexer_1_out0[28]));  // open: en, clr
  Register #(.width(32)) a1 (.D(DataWr), .Q(_5), .clk(demultiplexer_1_out0[5]));  // open: en, clr
  Register #(.width(32)) t5 (.D(DataWr), .Q(_13), .clk(demultiplexer_1_out0[13]));  // open: en, clr
  Register #(.width(32)) s5 (.D(DataWr), .Q(_21), .clk(demultiplexer_1_out0[21]));  // open: en, clr
  Register #(.width(32)) sp (.D(DataWr), .Q(_29), .clk(demultiplexer_1_out0[29]));  // open: en, clr
  Register #(.width(32)) a2 (.D(DataWr), .Q(_6), .clk(demultiplexer_1_out0[6]));  // open: en, clr
  Register #(.width(32)) t6 (.D(DataWr), .Q(_14), .clk(demultiplexer_1_out0[14]));  // open: en, clr
  Register #(.width(32)) s6 (.D(DataWr), .Q(_22), .clk(demultiplexer_1_out0[22]));  // open: en, clr
  Register #(.width(32)) fp (.D(DataWr), .Q(_30), .clk(demultiplexer_1_out0[30]));  // open: en, clr
  Register #(.width(32)) v0_2 (.D(DataWr), .Q(_7), .clk(demultiplexer_1_out0[7]));  // open: en, clr
  Register #(.width(32)) t7 (.D(DataWr), .Q(_15), .clk(demultiplexer_1_out0[15]));  // open: en, clr
  Register #(.width(32)) s7 (.D(DataWr), .Q(_23), .clk(demultiplexer_1_out0[23]));  // open: en, clr
  Register #(.width(32)) ra (.D(DataWr), .Q(_31), .clk(demultiplexer_1_out0[31]));  // open: en, clr
endmodule

module estensione_del_segno (
  input  [15:0] in_1,
  output [31:0] out_2
);


  assign out_2 = {{17{in_1[15]}}, in_1[14:0]};
endmodule

module alu (
  input  [31:0] in_1,
  input  [31:0] in_2,
  input  [2:0] ALUop,
  output zero,
  output [31:0] out_5
);

  wire [31:0] adder_1_out, and_1_out, bit_extender_1_out, bit_extender_2_out, not_1_out, or_1_out, xor_1_out;

  assign bit_extender_1_out = {{31{ALUop[2]}}, ALUop[2]};  // Bit_Extender bit_extender_1
  assign and_1_out = in_1 & in_2;  // AND_Gate and_1, 32 bits wide
  assign or_1_out = in_1 | in_2;  // OR_Gate or_1, 32 bits wide
  Adder #(.width(32)) adder_1 (.a(in_1), .b(xor_1_out), .out(adder_1_out), .cin(ALUop[2]));  // open: cout
  assign xor_1_out = in_2 ^ bit_extender_1_out;  // XOR_Gate xor_1, 32 bits wide
  assign bit_extender_2_out = {{31{1'b0}}, adder_1_out[31]};  // Bit_Extender bit_extender_2
  assign not_1_out = ~or_1_out;  // NOT_Gate not_1, 32 bits wide
  Multiplexer #(.select(3), .width(32), .enable("false")) multiplexer_1 (
    .in0(and_1_out), .in1(or_1_out), .in3(adder_1_out), .in4(not_1_out), .in6(adder_1_out),
    .in7(bit_extender_2_out), .out(out_5), .sel(ALUop));  // open: in2, in5
  nor nor_1 (zero, out_5[0], out_5[1], out_5[2], out_5[3], out_5[4], out_5[5], out_5[6], out_5[7], out_5[8], out_5[9], out_5[10], out_5[11], out_5[12], out_5[13], out_5[14], out_5[15], out_5[16], out_5[17], out_5[18], out_5[19], out_5[20], out_5[21], out_5[22], out_5[23], out_5[24], out_5[25], out_5[26], out_5[27], out_5[28], out_5[29], out_5[30], out_5[31]);
endmodule

module UC_ALU (
  input  [5:0] Funct,
  input  [2:0] ALUs,
  output [2:0] ALUop
);

  wire add_out, nor_out, or_out, R_out, slt_out, sub_out;
  wire [2:0] or_4_out;

  and add (add_out, ~Funct[0], ~Funct[1], ~Funct[2], ~Funct[3], ~Funct[4], Funct[5]);  // AND_Gate
  and sub (sub_out, ~Funct[0], Funct[1], ~Funct[2], ~Funct[3], ~Funct[4], Funct[5]);  // AND_Gate
  and slt (slt_out, ~Funct[0], Funct[1], ~Funct[2], Funct[3], ~Funct[4], Funct[5]);  // AND_Gate
  and \or  (or_out, Funct[0], ~Funct[1], Funct[2], ~Funct[3], ~Funct[4], Funct[5]);  // AND_Gate
  and \nor  (nor_out, Funct[0], Funct[1], Funct[2], ~Funct[3], ~Funct[4], Funct[5]);  // AND_Gate
  or or_2 (or_4_out[2], sub_out, slt_out, nor_out);
  or or_3 (or_4_out[1], add_out, sub_out, slt_out);
  or or_4 (or_4_out[0], add_out, slt_out, or_out);
  and R (R_out, ~ALUs[0], ALUs[1], ~ALUs[2]);  // AND_Gate
  Multiplexer #(.width(3), .enable("false")) multiplexer_1 (.in0(ALUs), .in1(or_4_out), .out(ALUop), .sel(R_out));
endmodule
